// Logisim project TinyCPU-Peripherals.circ as structural Verilog: 4 circuits, main circuit TinyCPUSystemMain
module TinyCPUSystemMain (
  input  CLK,
  input  RESET,
  input  INTERRUPT_REQUEST,
  output [15:0] OUTPUT_PORT_VALUE,
  output OUTPUT_PORT_VALID,
  output INTERRUPT_ENABLED,
  output INTERRUPT_PENDING,
  output IN_INTERRUPT_HANDLER,
  output [11:0] RETURN_ADDRESS,
  output RETURN_ADDRESS_VALID
);
endmodule

module OutputPort (
  input  [15:0] WRITE_VALUE,
  input  WRITE_VALID,
  input  WRITE_ENABLE,
  input  CLK,
  input  RESET,
  output [15:0] VALUE,
  output VALID
);

  Register #(.width(16)) OUTPUT_VALUE (.D(WRITE_VALUE), .en(WRITE_ENABLE), .clk(CLK), .Q(VALUE), .clr(RESET));
  Register #(.width(1)) OUTPUT_VALID (.D(WRITE_VALID), .en(WRITE_ENABLE), .clk(CLK), .Q(VALID), .clr(RESET));
endmodule

module OutputMemoryPath (
  input  [11:0] ADDRESS,
  input  [15:0] WRITE_VALUE,
  input  WRITE_VALID,
  input  WRITE_ENABLE,
  input  [15:0] RAM_READ_VALUE,
  input  RAM_READ_VALID,
  input  CLK,
  input  RESET,
  output [15:0] READ_VALUE,
  output READ_VALID,
  output RAM_WRITE_ENABLE,
  output [15:0] OUTPUT_PORT_VALUE,
  output OUTPUT_PORT_VALID
);

  wire comparator_1_eq, NOT_OUTPUT_ADDRESS_out, OUTPUT_WRITE_GATE_out, undriven;

  Comparator #(.width(12)) comparator_1 (.a({12{1'b1}}), .b(ADDRESS), .eq(comparator_1_eq));  // open: gt, lt
  not NOT_OUTPUT_ADDRESS (NOT_OUTPUT_ADDRESS_out, comparator_1_eq);
  buf RAM_WRITE_GATE (RAM_WRITE_ENABLE, NOT_OUTPUT_ADDRESS_out);  // AND_Gate
  buf OUTPUT_WRITE_GATE (OUTPUT_WRITE_GATE_out, NOT_OUTPUT_ADDRESS_out);  // AND_Gate
  Multiplexer #(.width(16)) multiplexer_1 (
    .in0(RAM_READ_VALUE), .in1(OUTPUT_PORT_VALUE), .out(READ_VALUE));  // open: sel
  Multiplexer multiplexer_2 (.in0(RAM_READ_VALID), .in1(OUTPUT_PORT_VALID), .out(READ_VALID), .sel(comparator_1_eq));
  Register #(.width(16)) register_1 (.D(WRITE_VALUE), .clk(CLK), .Q(OUTPUT_PORT_VALUE), .clr(undriven));  // open: en
  Register #(.width(1)) register_2 (
    .D(WRITE_VALID), .en(OUTPUT_WRITE_GATE_out), .clk(CLK), .Q(OUTPUT_PORT_VALID), .clr(undriven));
endmodule

module InterruptController (
  input  INTERRUPT_REQUEST,
  input  INSTRUCTION_BOUNDARY,
  input  ENABLE_REQUEST,
  input  DISABLE_REQUEST,
  input  RETURN_REQUEST,
  input  [11:0] NEXT_PC,
  input  CLK,
  input  RESET,
  output INTERRUPT_ACCEPT,
  output [11:0] TARGET_PC,
  output INTERRUPT_ENABLED,
  output INTERRUPT_PENDING,
  output IN_INTERRUPT_HANDLER,
  output [11:0] RETURN_ADDRESS,
  output RETURN_ADDRESS_VALID,
  output ILLEGAL_RETURN
);

  wire HANDLER_HOLD_out, MASK_CLEAR_NOT_out, MASK_CLEAR_REQUEST_out, MASK_HOLD_out, MASK_NEXT_out,
       MASK_SET_REQUEST_out, PENDING_HOLD_UNTIL_ACCEPT_out, PENDING_SET_OR_HOLD_out,
       PREVIOUS_REQUEST_NOT_out, REQUEST_LEVEL_q, RETURN_VALID_HOLD_p2, undriven, VALID_RETURN_GATE_out;
  wire [11:0] undriven_2;

  or PENDING_SET_OR_HOLD (PENDING_SET_OR_HOLD_out, DISABLE_REQUEST, DISABLE_REQUEST);
  or MASK_SET_REQUEST (MASK_SET_REQUEST_out, DISABLE_REQUEST, DISABLE_REQUEST);
  buf MASK_CLEAR_REQUEST (MASK_CLEAR_REQUEST_out, DISABLE_REQUEST);  // OR_Gate
  Register #(.width(1)) REQUEST_LEVEL (
    .D(INTERRUPT_REQUEST), .en(INSTRUCTION_BOUNDARY), .clk(CLK), .Q(REQUEST_LEVEL_q), .clr(RESET));
  Register #(.width(1)) register_1 (.D(MASK_NEXT_out), .en(1'b1), .clk(CLK), .Q(RESET), .clr(RESET));
  Register #(.width(1)) register_2 (
    .D(PENDING_SET_OR_HOLD_out), .en(DISABLE_REQUEST), .clk(PENDING_HOLD_UNTIL_ACCEPT_out),
    .Q(DISABLE_REQUEST), .clr(RESET));
  Register #(.width(1)) register_3 (.D(undriven), .en(RESET), .clk(CLK), .Q(DISABLE_REQUEST), .clr(RESET));
  Register #(.width(12)) register_4 (
    .D(NEXT_PC), .en(RESET), .clk(CLK), .Q({RETURN_ADDRESS[11:1], ILLEGAL_RETURN}), .clr(RESET));
  Register #(.width(1)) register_5 (.D(RESET), .en(CLK), .clk(RESET), .Q(RETURN_ADDRESS_VALID), .clr(RESET));
  // NOT_Gate MASK_CLEAR_NOT has open pins: in=open, out=MASK_CLEAR_NOT_out
  not PREVIOUS_REQUEST_NOT (PREVIOUS_REQUEST_NOT_out, REQUEST_LEVEL_q);
  not NOT_IN_HANDLER (DISABLE_REQUEST, DISABLE_REQUEST);
  and MASK_HOLD (MASK_HOLD_out, RESET, MASK_CLEAR_NOT_out);
  buf RISING_EDGE_DETECT (DISABLE_REQUEST, PREVIOUS_REQUEST_NOT_out);  // AND_Gate
  buf INTERRUPT_ACCEPT_GATE (RESET, DISABLE_REQUEST);  // AND_Gate
  // AND_Gate ILLEGAL_RETURN_GATE has open pins: in0=DISABLE_REQUEST, in1=DISABLE_REQUEST, out=open
  and PENDING_HOLD_UNTIL_ACCEPT (PENDING_HOLD_UNTIL_ACCEPT_out, DISABLE_REQUEST, DISABLE_REQUEST);
  buf MASK_NEXT (MASK_NEXT_out, MASK_HOLD_out);  // OR_Gate
  and VALID_RETURN_GATE (VALID_RETURN_GATE_out, DISABLE_REQUEST, ILLEGAL_RETURN);
  // AND_Gate RETURN_VALID_HOLD: pin names not known; wires that end beside it: {RETURN_ADDRESS[11:1], ILLEGAL_RETURN}, RETURN_VALID_HOLD_p2
  // AND_Gate HANDLER_HOLD has open pins: out=HANDLER_HOLD_out
  not INTERRUPT_ACCEPT_NOT (ILLEGAL_RETURN, RESET);
  Multiplexer #(.width(12)) multiplexer_1 (
    .in0(undriven_2), .in1({RETURN_ADDRESS[11:1], ILLEGAL_RETURN}),
    .out({RETURN_ADDRESS[11:1], ILLEGAL_RETURN}), .sel(DISABLE_REQUEST));
  not VALID_RETURN_NOT (RETURN_VALID_HOLD_p2, VALID_RETURN_GATE_out);
  // OR_Gate RETURN_VALID_NEXT has open pins: in0=ILLEGAL_RETURN, out=open
  // OR_Gate HANDLER_NEXT has open pins: in1=HANDLER_HOLD_out, out=open
  // Pins of 1 and 12 bits meet at {RETURN_ADDRESS[11:1], ILLEGAL_RETURN}

  assign ENABLE_REQUEST = DISABLE_REQUEST;
  assign IN_INTERRUPT_HANDLER = DISABLE_REQUEST;
  assign INTERRUPT_ACCEPT = RESET;
  assign INTERRUPT_ENABLED = RESET;
  assign INTERRUPT_PENDING = DISABLE_REQUEST;
  assign RETURN_ADDRESS[0] = ILLEGAL_RETURN;
  assign RETURN_REQUEST = DISABLE_REQUEST;
  assign TARGET_PC = {RETURN_ADDRESS[11:1], ILLEGAL_RETURN};
  // also tied to VCC on the sheet: {DISABLE_REQUEST, INSTRUCTION_BOUNDARY}
endmodule
