// Logisim project TinyCPU_Peripherals.circ as structural Verilog: 4 circuits, main circuit TinyCPUSystemMain
module TinyCPUSystemMain (
  input  CLK,
  input  RESET,
  input  INTERRUPT_REQUEST,
  output [15:0] OUTPUT_PORT_VALUE,
  output OUTPUT_PORT_VALID,
  output INTERRUPT_ENABLED,
  output INTERRUPT_PENDING,
  output IN_INTERRUPT_HANDLER,
  output [11:0] RETURN_ADDRESS,
  output RETURN_ADDRESS_VALID
);
endmodule

module OutputPort (
  input  [15:0] WRITE_VALUE,
  input  WRITE_VALID,
  input  WRITE_ENABLE,
  input  CLK,
  input  RESET,
  output [15:0] VALUE,
  output VALID
);

  wire OUTPUT_WRITE_ACCEPTED_out;

  Register #(.width(16)) OUTPUT_VALUE (
    .D(WRITE_VALUE), .en(OUTPUT_WRITE_ACCEPTED_out), .clk(CLK), .Q(VALUE), .clr(RESET));
  and OUTPUT_WRITE_ACCEPTED (OUTPUT_WRITE_ACCEPTED_out, WRITE_VALID, WRITE_ENABLE);
  Register #(.width(1)) OUTPUT_VALID (
    .D(WRITE_VALID), .en(OUTPUT_WRITE_ACCEPTED_out), .clk(CLK), .Q(VALID), .clr(RESET));
endmodule

module OutputMemoryPath (
  input  [15:0] RAM_READ_VALUE,
  input  RAM_READ_VALID,
  input  [11:0] ADDRESS,
  input  [15:0] WRITE_VALUE,
  input  WRITE_VALID,
  input  WRITE_ENABLE,
  input  CLK,
  input  RESET,
  output [15:0] READ_VALUE,
  output READ_VALID,
  output [15:0] OUTPUT_PORT_VALUE,
  output OUTPUT_PORT_VALID,
  output RAM_WRITE_ENABLE
);

  wire OUTPUT_ADDRESS_DECODE_eq, OUTPUT_WRITE_GATE_out;

  Comparator #(.width(12)) OUTPUT_ADDRESS_DECODE (
    .a(ADDRESS), .b({12{1'b1}}), .eq(OUTPUT_ADDRESS_DECODE_eq));  // open: gt, lt
  and OUTPUT_WRITE_GATE (OUTPUT_WRITE_GATE_out, WRITE_VALID, OUTPUT_ADDRESS_DECODE_eq, WRITE_ENABLE);
  and RAM_WRITE_GATE (RAM_WRITE_ENABLE, ~OUTPUT_ADDRESS_DECODE_eq, WRITE_ENABLE);  // AND_Gate
  Register #(.width(16)) OUTPUT_VALUE (
    .D(WRITE_VALUE), .en(OUTPUT_WRITE_GATE_out), .clk(CLK), .Q(OUTPUT_PORT_VALUE), .clr(RESET));
  Register #(.width(1)) OUTPUT_VALID (
    .D(WRITE_VALID), .en(OUTPUT_WRITE_GATE_out), .clk(CLK), .Q(OUTPUT_PORT_VALID), .clr(RESET));
  Multiplexer #(.width(16)) OUTPUT_READ_VALUE_SELECT (
    .in0(RAM_READ_VALUE), .in1(OUTPUT_PORT_VALUE), .out(READ_VALUE), .sel(OUTPUT_ADDRESS_DECODE_eq));
  Multiplexer OUTPUT_READ_VALID_SELECT (
    .in0(RAM_READ_VALID), .in1(OUTPUT_PORT_VALID), .out(READ_VALID), .sel(OUTPUT_ADDRESS_DECODE_eq));

  // Notes on the sheet:
  //   OUTPUT MEMORY PATH — address 0xFFF selects output port
endmodule

module InterruptController (
  input  INTERRUPT_REQUEST,
  input  INSTRUCTION_BOUNDARY,
  input  ENABLE_REQUEST,
  input  DISABLE_REQUEST,
  input  RETURN_REQUEST,
  input  [11:0] NEXT_PC,
  input  RESET,
  input  CLK,
  output INTERRUPT_ACCEPT,
  output INTERRUPT_PENDING,
  output INTERRUPT_ENABLED,
  output ILLEGAL_RETURN,
  output [11:0] RETURN_ADDRESS,
  output [11:0] TARGET_PC,
  output RETURN_ADDRESS_VALID,
  output IN_INTERRUPT_HANDLER
);

  wire HANDLER_HOLD_out, HANDLER_NEXT_out, MASK_HOLD_out, MASK_NEXT_out, PENDING_HOLD_UNTIL_ACCEPT_out,
       PENDING_SET_OR_HOLD_out, REQUEST_LEVEL_q, RETURN_VALID_HOLD_out, RETURN_VALID_NEXT_out,
       RISING_EDGE_DETECT_out, VALID_RETURN_GATE_out;

  and RISING_EDGE_DETECT (RISING_EDGE_DETECT_out, ~REQUEST_LEVEL_q, INTERRUPT_REQUEST);  // AND_Gate
  and PENDING_HOLD_UNTIL_ACCEPT (PENDING_HOLD_UNTIL_ACCEPT_out, INTERRUPT_PENDING, ~INTERRUPT_ACCEPT);  // AND_Gate
  and MASK_HOLD (MASK_HOLD_out, INTERRUPT_ENABLED, ~DISABLE_REQUEST, ~INTERRUPT_ACCEPT);  // AND_Gate
  and RETURN_VALID_HOLD (RETURN_VALID_HOLD_out, RETURN_ADDRESS_VALID, ~VALID_RETURN_GATE_out);  // AND_Gate
  and HANDLER_HOLD (HANDLER_HOLD_out, IN_INTERRUPT_HANDLER, ~VALID_RETURN_GATE_out);  // AND_Gate
  or PENDING_SET_OR_HOLD (PENDING_SET_OR_HOLD_out, RISING_EDGE_DETECT_out, PENDING_HOLD_UNTIL_ACCEPT_out);
  or MASK_NEXT (MASK_NEXT_out, ENABLE_REQUEST, VALID_RETURN_GATE_out, MASK_HOLD_out);
  or RETURN_VALID_NEXT (RETURN_VALID_NEXT_out, INTERRUPT_ACCEPT, RETURN_VALID_HOLD_out);
  or HANDLER_NEXT (HANDLER_NEXT_out, INTERRUPT_ACCEPT, HANDLER_HOLD_out);
  Register #(.width(1)) REQUEST_LEVEL (.D(INTERRUPT_REQUEST), .en(1'b1), .clk(CLK), .Q(REQUEST_LEVEL_q), .clr(RESET));
  Register #(.width(1)) u_INTERRUPT_PENDING (
    .D(PENDING_SET_OR_HOLD_out), .en(1'b1), .clk(CLK), .Q(INTERRUPT_PENDING), .clr(RESET));
  Register #(.width(1)) u_INTERRUPT_ENABLED (
    .D(MASK_NEXT_out), .en(1'b1), .clk(CLK), .Q(INTERRUPT_ENABLED), .clr(RESET));
  Register #(.width(12)) u_RETURN_ADDRESS (
    .D(NEXT_PC), .en(INTERRUPT_ACCEPT), .clk(CLK), .Q(RETURN_ADDRESS), .clr(RESET));
  Register #(.width(1)) u_RETURN_ADDRESS_VALID (
    .D(RETURN_VALID_NEXT_out), .en(1'b1), .clk(CLK), .Q(RETURN_ADDRESS_VALID), .clr(RESET));
  Register #(.width(1)) u_IN_INTERRUPT_HANDLER (
    .D(HANDLER_NEXT_out), .en(1'b1), .clk(CLK), .Q(IN_INTERRUPT_HANDLER), .clr(RESET));
  and INTERRUPT_ACCEPT_GATE (INTERRUPT_ACCEPT, INSTRUCTION_BOUNDARY, INTERRUPT_PENDING, INTERRUPT_ENABLED, ~IN_INTERRUPT_HANDLER);  // AND_Gate
  and VALID_RETURN_GATE (VALID_RETURN_GATE_out, RETURN_REQUEST, RETURN_ADDRESS_VALID, IN_INTERRUPT_HANDLER);
  and ILLEGAL_RETURN_GATE (ILLEGAL_RETURN, RETURN_REQUEST, ~VALID_RETURN_GATE_out);  // AND_Gate
  Multiplexer #(.width(12)) INTERRUPT_TARGET_SELECT (
    .in0(12'hff0), .in1(RETURN_ADDRESS), .out(TARGET_PC), .sel(VALID_RETURN_GATE_out));

  // Notes on the sheet:
  //   EDGE / INPUTS
  //   NEXT-STATE LOGIC
  //   feedback buses: ACCEPT / VALID_RETURN
  //   STATE REGISTERS
  //   ACCEPT / RETURN DECODE
endmodule
